# Fritzing sketch intaiSketch (saved by Fritzing 0.9.3b)
breadboards: 1

parts:
  MH-ET_LIVE_ESP32_DEVKIT1 = MH-ET LIVE ESP32 DEVKIT 38 pins
  Part1 = Adafruit MAX4466 Electret Microphone Amplifier [part_number="Adafruit #1063"]
  Part2 = Adafruit MAX4466 Electret Microphone Amplifier [part_number="Adafruit #1063"]
  Part3 = Adafruit MAX4466 Electret Microphone Amplifier [part_number="Adafruit #1063"]
  Part4 = Adafruit MAX4466 Electret Microphone Amplifier [part_number="Adafruit #1063"]
  Part5 = DC-DC Power Module (5v)
  LED2 = smd LED [color="Red (633nm)" package="1206 [SMD]"]
  LED3 = smd LED [color="Red (633nm)" package="0805 [SMD]"]
  Part6 = Solar Panel [package="Renogy 50 Watts 12 Volt Monocrystalline Bendable Solar Panel"]
  BAT3 = 12 battery [package=battery]
  Part7 = Solar Charge Controller [part_number="HGX Series Solar Charge Controller PWM" package=PWM-Model]
  C1 = Electrolytic Capacitor [package="8mm [THT, electrolytic]"]
  C2 = Electrolytic Capacitor [package="8mm [THT, electrolytic]"]
  C3 = Electrolytic Capacitor [package="8mm [THT, electrolytic]"]
  C4 = Electrolytic Capacitor [package="8mm [THT, electrolytic]"]
  M1 = Osoyoo SX1278-ra-02
  D1 = Rectifier Diode [part_number=1N4001 package="300 mil [THT]"]
  SD_card_module1 = SD Card Module

nets:
  N1: MH-ET_LIVE_ESP32_DEVKIT1.IO34, Part4.OUT
  N2: MH-ET_LIVE_ESP32_DEVKIT1.IO35, Part3.OUT
  N3: MH-ET_LIVE_ESP32_DEVKIT1.IO32, Part2.OUT
  N4: MH-ET_LIVE_ESP32_DEVKIT1.IO33, Part1.OUT
  N5: MH-ET_LIVE_ESP32_DEVKIT1.IO25, SD_card_module1.CS
  N6: MH-ET_LIVE_ESP32_DEVKIT1.IO26, LED2.anode
  N7: MH-ET_LIVE_ESP32_DEVKIT1.IO27, LED3.anode
  N8: MH-ET_LIVE_ESP32_DEVKIT1.IO14, M1.RST
  N9: MH-ET_LIVE_ESP32_DEVKIT1.IO12, SD_card_module1.MISO
  GND: MH-ET_LIVE_ESP32_DEVKIT1.GND, Part1.GND, Part2.GND, Part3.GND, Part4.GND, Part5.GND*, LED2.cathode, LED3.cathode, C1.-, C2.-, C3.-, C4.-, M1.GND, SD_card_module1.GND
  N10: MH-ET_LIVE_ESP32_DEVKIT1.IO13, SD_card_module1.MOSI
  VCC: MH-ET_LIVE_ESP32_DEVKIT1.5V, Part1.VCC, Part2.VCC, Part3.VCC, Part4.VCC, C1.+, C2.+, C3.+, C4.+, M1.3.3V, D1.cathode, SD_card_module1.+5
  N11: MH-ET_LIVE_ESP32_DEVKIT1.IO23, M1.MOSI
  N12: MH-ET_LIVE_ESP32_DEVKIT1.IO19, M1.MISO
  N13: MH-ET_LIVE_ESP32_DEVKIT1.IO18, M1.SCK
  N14: MH-ET_LIVE_ESP32_DEVKIT1.IO5, M1.NSS
  N15: MH-ET_LIVE_ESP32_DEVKIT1.IO2, M1.DIO0
  N16: MH-ET_LIVE_ESP32_DEVKIT1.IO15, SD_card_module1.SCK
  N17: Part5.Vin, Part7.Connector_5
  N18: Part5.GND, Part7.Connector_6
  N19: Part5.Vout, D1.anode
  N20: Part6.Connector_1, Part7.Connector_1
  N21: Part6.Connector_2, Part7.Connector_2
  N22: BAT3.-, Part7.Connector_4
  N23: BAT3.+, Part7.Connector_3

custom parts:
  MH-ET LIVE ESP32 DEVKIT 38 pins: http://mh.nodebb.com/topic/2/mh-et-live-esp32-devkit
  Adafruit MAX4466 Electret Microphone Amplifier: Add an ear to your project with this well-designed electret microphone amplifier. This fully assembled and tested board comes with a 20-20KHz electret microphone soldered on. For the amplification, we use the Maxim MAX4466, an op-amp specifically designed for this delicate task! The amplifier has excellent power supply noise rejection, so this amplifier sounds really good and isn't nearly as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
  DC-DC Power Module (5v): DC-DC Power Module based con AMS1117-5.0 Input: DC 6~12V (input power must higher 1V than output power); Output: 5V (+/-0.05V error), 800mA
  Solar Panel: Renogy 50 Watts 12 Volt Solar Panel
  12 battery: 12V lead acid type battery, like the Husqvarna YTH2448 12V 35AH battery. This is the mini version 1/4 the size of the actual battery to be closer to typical breadboard parts (around 2in wide rathher than 7in). The pads in pcb are sized to accomidate up to 14ga wire (as these batterys will deliver high currents.)
  Solar Charge Controller: PWM-Solar Charge Controller
  Electrolytic Capacitor: electrolytic capacitor, 8mm dia
  Osoyoo SX1278-ra-02: Osoyoo Long Distance wireless transceiver Uart LoRa Module.
  SD Card Module: SD Card Module Slot Socket Reader For Arduino ARM MCU
