# Fritzing sketch intaiSketch (saved by Fritzing 0.9.3b)
breadboards: 1

parts:
  ESP32_DEV_KIT = MH-ET LIVE ESP32 DEVKIT 38 pins
  Lora = Osoyoo SX1278-ra-02
  Jack_Power = Power Jack [package=power_jack_smd]
  Modul_Stepdown = DC-DC Power Module (5v)

nets:
  3V3: ESP32_DEV_KIT.3V3, Lora.3.3V, Modul_Stepdown.Vout
  N1: ESP32_DEV_KIT.IO14, Lora.RST
  GND: ESP32_DEV_KIT.GND, Lora.GND, Modul_Stepdown.GND*
  N2: ESP32_DEV_KIT.IO23, Lora.MOSI
  N3: ESP32_DEV_KIT.IO19, Lora.MISO
  N4: ESP32_DEV_KIT.IO18, Lora.SCK
  N5: ESP32_DEV_KIT.IO5, Lora.NSS
  GND_2: Jack_Power.GND, Modul_Stepdown.GND
  N6: Jack_Power.GNDBREAK, Modul_Stepdown.Vin

custom parts:
  MH-ET LIVE ESP32 DEVKIT 38 pins: http://mh.nodebb.com/topic/2/mh-et-live-esp32-devkit
  Osoyoo SX1278-ra-02: Osoyoo Long Distance wireless transceiver Uart LoRa Module.
  DC-DC Power Module (5v): DC-DC Power Module based con AMS1117-5.0 Input: DC 6~12V (input power must higher 1V than output power); Output: 5V (+/-0.05V error), 800mA
